# Fritzing sketch otopark (saved by Fritzing 0.9.3b)
circuit board: 8.46667cm x 5.64444cm
breadboards: 2

parts:
  Part1 = Arduino Mega 2560 (Rev3)
  hc-sr2 = hc-sr04
  LED2 = LED - 5mm [color="Green (570nm)" package="5 mm [THT]"]
  R1 = Resistor [tolerance=±5% resistance=220 package="2010 [SMD]"]
  R2 = Resistor [tolerance=±5% resistance=220 package="2010 [SMD]"]
  LED3 = LED - 5mm [color="Red (635nm)" package="5 mm [THT]"]
  J1 = Basic Servo
  hc-sr3 = hc-sr04
  LED4 = LED - 5mm [color="Red (635nm)" package="5 mm [THT]"]
  LED5 = LED - 5mm [color="Green (570nm)" package="5 mm [THT]"]
  R3 = Resistor [tolerance=±5% resistance=220 package="2010 [SMD]"]
  R4 = Resistor [tolerance=±5% resistance=220 package="2010 [SMD]"]
  hc-sr4 = hc-sr04
  LED6 = LED - 5mm [color="Red (635nm)" package="5 mm [THT]"]
  LED7 = LED - 5mm [color="Green (570nm)" package="5 mm [THT]"]
  R5 = Resistor [tolerance=±5% resistance=220 package="2010 [SMD]"]
  R6 = Resistor [tolerance=±5% resistance=220 package="2010 [SMD]"]
  hc-sr5 = hc-sr04
  LED8 = LED - 5mm [color="Red (635nm)" package="5 mm [THT]"]
  LED9 = LED - 5mm [color="Green (570nm)" package="5 mm [THT]"]
  R7 = Resistor [tolerance=±5% resistance=220 package="2010 [SMD]"]
  R8 = Resistor [tolerance=±5% resistance=220 package="2010 [SMD]"]
  U1 = ESP8266 NodeMCU LoLin module
  Part2 = LCD1602-I2C

nets (from the breadboard view):
  N1: Part1.D17_PWM/RX2, U1.D6
  N2: Part1.D16_PWM/TX2, U1.D5
  N3: Part1.SCL, Part2.SCL
  N4: Part1.SDA, Part2.SDA
  GND: Part1.GND, hc-sr2.GND, LED2.cathode, LED3.cathode, J1.gnd, hc-sr3.GND, LED4.cathode, LED5.cathode, LED6.cathode, LED7.cathode, hc-sr5.GND, LED8.cathode, LED9.cathode, U1.GND, Part2.GND
  N5: Part1.D9_PWM, J1.pulse
  VCC: Part1.5V, hc-sr2.VCC, J1.vcc, hc-sr3.VCC, hc-sr5.VCC, U1.Vin, Part2.VCC
  N6: Part1.D24, R1.Pin_0
  N7: Part1.D25, R2.Pin_0
  N8: Part1.D26, hc-sr2.Trig
  N9: Part1.D27, hc-sr2.Echo
  N10: Part1.D28, R4.Pin_0
  N11: Part1.D29, R3.Pin_0
  N12: Part1.D30, hc-sr3.Trig
  N13: Part1.D31, hc-sr3.Echo
  N14: Part1.D34, R6.Pin_0
  N15: Part1.D35, R5.Pin_0
  N16: Part1.D36, hc-sr4.Trig
  N17: Part1.D37, hc-sr4.Echo
  N18: Part1.D40, R8.Pin_0
  N19: Part1.D41, R7.Pin_0
  N20: Part1.D42, hc-sr5.Trig
  N21: Part1.D43, hc-sr5.Echo
  N22: LED2.anode, R1.Pin_1
  N23: R2.Pin_1, LED3.anode
  N24: LED4.anode, R3.Pin_1
  N25: LED5.anode, R4.Pin_1
  N26: LED6.anode, R5.Pin_1
  N27: LED7.anode, R6.Pin_1
  N28: LED8.anode, R7.Pin_1
  N29: LED9.anode, R8.Pin_1

custom parts:
  ESP8266 NodeMCU LoLin module: ESP8266 based NodeMCU
  LCD1602-I2C: A standard character display, usually with 2x16 characters. Comes in many colors with LCM1602 IIC attached.
